# Fritzing sketch UDNeuroinjector_UNO_Fritizing (saved by Fritzing 1.0.6)
breadboards: 1

parts:
  Part1 = Arduino Uno (Rev3) - ICSP
  R1 = Resistor [tolerance=±5% power=0.25W resistance=22 package=THT]
  JL012-13-5_1 = JL012-13-5.2 Lever (Limit) Switch SPDT + NO + NC [part_number=JL012-13-5.2]
  S1 = Pushbutton [package="[SMD]"]
  Mod1 = TMC2209 [package=THT]
  R2 = Resistor [tolerance=±5% power=0.25W resistance=22 package=THT]
  Part2 = Black Joystick KY-023
  M1 = Stepper Motor - Bipolar  # not connected

nets:
  N1: Part1.A1, Part2.VRx
  N2: Part1.ICSP_MISO, Part1.D12/MISO, R1.Pin_1, JL012-13-5_1.NO
  N3: Part1.D8, Mod1.Step
  N4: Part1.D9_PWM, Mod1.Dir
  N5: Part1.D13/SCK, S1.Pin_1, S1.Pin_2, R2.Pin_1
  GND: Part1.GND, R1.Pin_0, Mod1.GND, Mod1.EN, R2.Pin_0, Part2.GND
  5V: Part1.5V, JL012-13-5_1.NC, S1.Pin_3, S1.Pin_4, Mod1.VDD, Mod1.VM, Part2.+5V
  N6: Mod1.MS2, Mod1.MS1

custom parts:
  JL012-13-5.2 Lever (Limit) Switch SPDT + NO + NC: Micro Switch; Model No.: JL012-13.5-2; Actuator Action: Momentary; Actuator Type: Hinge Lever; Contact Configuration: 1NO, 1NC (SPDT) Temperature -25~65℃；Relative humidity: below 85%; Rate Voltage: 125V AC; Rated Current: 1A.
  TMC2209: TMC2209-LA stepper motor controller and driver. Supply voltage 4.75-28V Iphase up to 1.77A rms (2.5A peak)
  Black Joystick KY-023: Description: The joystick is a combination of 2 analoog potentiometer and a digital switch. Arduino GND --> Module pin - Arduino +5V --> Module pin +5V Arduino Analoog 0 --> Module VRx Arduino Analoog 1 --> Module VRy Arduino Digital --> Module SW Dimensions: 1" x 1.25"
